// Logisim project Computador.circ as structural Verilog: 4 circuits, main circuit main
module main (
  input  in_1,
  input  in_2,
  input  in_3,
  input  in_4,
  input  in_5,
  input  in_6,
  input  in_7,
  input  in_8,
  input  in_9,
  input  in_10,
  input  in_11,
  input  in_12,
  input  in_13,
  input  in_14,
  input  in_15,
  input  in_16,
  input  in_17,
  input  in_18,
  input  in_19,
  input  in_20,
  output out_21,
  output out_22,
  output out_23,
  output out_24
);

  wire and_1_out, and_2_out, and_3_out, and_4_out, and_5_out, and_6_out, and_7_out, and_8_out, and_9_out,
       and_10_out, and_11_out, and_12_out, and_13_out, and_14_out, and_15_out, and_16_out, and_17_out,
       and_18_out, and_19_out, and_20_out, and_21_out, and_22_out, and_23_out, and_24_out, and_25_out,
       and_26_out, and_27_out, and_28_out, and_29_out, and_30_out, and_31_out, and_34_out, clock_1_out,
       convert_1_a2, convert_1_b, convert_1_c2, convert_1_d2, convert_1_e, convert_1_f, convert_1_g,
       convert_2_a2, convert_2_b, convert_2_c2, convert_2_d2, convert_2_e, convert_2_f, convert_2_g,
       convert_3_a2, convert_3_b, convert_3_c2, convert_3_d2, convert_3_e, convert_3_f, convert_3_g,
       d_ff_1_q, d_ff_2_q, d_ff_3_q, d_ff_4_q, multiplica_1_p0, multiplica_1_p1, multiplica_1_p2,
       multiplica_1_p3, or_1_out, or_2_out, or_3_out, or_4_out, or_5_out, or_6_out, or_7_out, or_8_out,
       or_9_out, or_10_out, soma_1_carry_in, soma_1_carry_out, soma_1_s0, soma_1_s1, t_ff_1_q, t_ff_2_q,
       t_ff_2_qn;

  Clock clock_1 (.out(clock_1_out));
  T_Flip_Flop t_ff_1 (.clk(t_ff_2_qn), .T(in_1), .Q(t_ff_1_q));  // open: Qn, preset, reset, en
  and and_1 (and_1_out, ~t_ff_2_q, ~t_ff_1_q);  // AND_Gate
  and and_2 (and_2_out, t_ff_2_q, ~t_ff_1_q);  // AND_Gate
  and and_3 (and_3_out, ~t_ff_2_q, t_ff_1_q);  // AND_Gate
  T_Flip_Flop t_ff_2 (.clk(clock_1_out), .T(in_1), .Q(t_ff_2_q), .Qn(t_ff_2_qn));  // open: preset, reset, en
  and and_4 (and_4_out, and_1_out, in_3);
  and and_5 (and_5_out, and_1_out, in_2);
  and and_6 (and_6_out, and_2_out, in_8);
  and and_7 (and_7_out, and_2_out, in_9);
  and and_8 (and_8_out, and_3_out, in_16);
  and and_9 (and_9_out, and_3_out, in_15);
  and and_10 (and_10_out, and_1_out, in_5);
  and and_11 (and_11_out, and_1_out, in_4);
  and and_12 (and_12_out, and_2_out, in_11);
  and and_13 (and_13_out, and_2_out, in_10);
  and and_14 (and_14_out, and_3_out, in_17);
  and and_15 (and_15_out, and_1_out, in_6);
  and and_16 (and_16_out, and_2_out, in_12);
  and and_17 (and_17_out, and_3_out, in_18);
  and and_18 (and_18_out, and_3_out, in_19);
  and and_19 (and_19_out, and_1_out, in_7);
  and and_20 (and_20_out, and_2_out, in_13);
  and and_21 (and_21_out, and_3_out, in_20);
  or or_1 (or_1_out, and_5_out, and_6_out, and_9_out);
  or or_2 (or_2_out, and_4_out, and_7_out, and_8_out);
  or or_3 (or_3_out, and_11_out, and_13_out, and_14_out);
  or or_4 (or_4_out, and_10_out, and_12_out, and_17_out);
  or or_5 (or_5_out, and_15_out, and_16_out, and_18_out);
  or or_6 (or_6_out, and_19_out, and_20_out, and_21_out);
  convert convert_1 (
    .A(in_14), .B2(in_14), .C(or_3_out), .D(or_4_out), .B(convert_1_b), .A2(convert_1_a2), .F(convert_1_f),
    .G(convert_1_g), .E(convert_1_e), .D2(convert_1_d2), .C2(convert_1_c2));
  _7_Segment_Display u_7_segment_display_1 (
    .g(convert_1_g), .f(convert_1_f), .a(convert_1_a2), .b(convert_1_b), .e(convert_1_e), .d(convert_1_d2),
    .c(convert_1_c2));  // open: dp
  and and_22 (and_22_out, or_5_out, ~or_6_out);  // AND_Gate
  and and_23 (and_23_out, or_4_out, and_22_out);
  convert convert_2 (
    .A(in_14), .B2(in_14), .C(or_1_out), .D(or_2_out), .B(convert_2_b), .A2(convert_2_a2), .F(convert_2_f),
    .G(convert_2_g), .E(convert_2_e), .D2(convert_2_d2), .C2(convert_2_c2));
  _7_Segment_Display u_7_segment_display_2 (
    .g(convert_2_g), .f(convert_2_f), .a(convert_2_a2), .b(convert_2_b), .e(convert_2_e), .d(convert_2_d2),
    .c(convert_2_c2));  // open: dp
  and and_24 (and_24_out, or_3_out, and_22_out);
  and and_25 (and_25_out, or_2_out, and_22_out);
  soma soma_1 (
    .a(and_26_out), .b(and_25_out), .c(and_24_out), .d(and_23_out), .s1(soma_1_s1), .s0(soma_1_s0),
    .carry_in(soma_1_carry_in), .carry_out(soma_1_carry_out));
  and and_26 (and_26_out, or_1_out, and_22_out);
  or or_7 (or_7_out, soma_1_carry_out, multiplica_1_p0);
  or or_8 (or_8_out, soma_1_carry_in, multiplica_1_p1);
  convert convert_3 (
    .A(or_10_out), .B2(or_9_out), .C(or_8_out), .D(or_7_out), .B(convert_3_b), .A2(convert_3_a2),
    .F(convert_3_f), .G(convert_3_g), .E(convert_3_e), .D2(convert_3_d2), .C2(convert_3_c2));
  _7_Segment_Display u_7_segment_display_3 (
    .g(convert_3_g), .f(convert_3_f), .a(convert_3_a2), .b(convert_3_b), .e(convert_3_e), .d(convert_3_d2),
    .c(convert_3_c2));  // open: dp
  and and_27 (and_27_out, ~or_5_out, or_6_out);  // AND_Gate
  and and_28 (and_28_out, or_4_out, and_27_out);
  and and_29 (and_29_out, or_3_out, and_27_out);
  or or_9 (or_9_out, soma_1_s0, multiplica_1_p2);
  or or_10 (or_10_out, soma_1_s1, multiplica_1_p3);
  and and_30 (and_30_out, or_1_out, and_27_out);
  and and_31 (and_31_out, or_2_out, and_27_out);
  multiplica multiplica_1 (
    .a(and_30_out), .b(and_31_out), .c(and_29_out), .d(and_28_out), .p3(multiplica_1_p3),
    .p2(multiplica_1_p2), .p1(multiplica_1_p1), .p0(multiplica_1_p0));
  D_Flip_Flop d_ff_1 (.clk(clock_1_out), .D(or_10_out), .Q(d_ff_1_q));  // open: Qn, preset, en, reset
  and and_32 (out_21, d_ff_1_q, and_34_out);
  D_Flip_Flop d_ff_2 (.clk(clock_1_out), .D(or_9_out), .Q(d_ff_2_q));  // open: Qn, preset, en, reset
  and and_33 (out_22, d_ff_2_q, and_34_out);
  and and_34 (and_34_out, or_5_out, or_6_out);
  D_Flip_Flop d_ff_3 (.clk(clock_1_out), .D(or_8_out), .Q(d_ff_3_q));  // open: Qn, preset, en, reset
  and and_35 (out_23, d_ff_3_q, and_34_out);
  D_Flip_Flop d_ff_4 (.clk(clock_1_out), .D(or_7_out), .Q(d_ff_4_q));  // open: Qn, preset, en, reset
  and and_36 (out_24, d_ff_4_q, and_34_out);
endmodule

module convert (
  input  A,
  input  B2,
  input  C,
  input  D,
  output B,
  output A2,
  output F,
  output G,
  output E,
  output D2,
  output C2
);

  wire and_1_out, and_2_out, and_3_out, and_4_out, and_5_out, and_6_out, and_7_out, and_8_out, and_9_out,
       and_10_out, and_11_out, and_12_out, and_13_out, and_14_out, and_15_out, and_16_out, and_17_out,
       not_1_out, not_2_out, not_3_out, not_4_out, not_5_out, not_6_out, not_7_out, not_8_out, not_9_out,
       not_10_out, not_11_out, not_12_out, not_13_out, not_14_out, not_15_out, not_16_out, not_17_out,
       not_18_out, not_19_out, not_20_out, not_21_out, not_22_out;

  not not_1 (not_1_out, B2);
  not not_2 (not_2_out, C);
  and and_1 (and_1_out, not_2_out, not_3_out);
  not not_3 (not_3_out, D);
  and and_2 (and_2_out, C, D);
  not not_4 (not_4_out, B2);
  and and_3 (and_3_out, not_4_out, not_5_out);
  not not_5 (not_5_out, D);
  and and_4 (and_4_out, B2, D);
  not not_6 (not_6_out, C);
  and and_5 (and_5_out, not_6_out, not_7_out);
  not not_7 (not_7_out, D);
  and and_6 (and_6_out, B2, not_8_out);
  not not_8 (not_8_out, C);
  and and_7 (and_7_out, B2, not_9_out);
  not not_9 (not_9_out, D);
  not not_10 (not_10_out, B2);
  and and_8 (and_8_out, not_10_out, C);
  and and_9 (and_9_out, B2, not_11_out);
  not not_11 (not_11_out, C);
  and and_10 (and_10_out, B2, not_12_out);
  not not_12 (not_12_out, D);
  not not_13 (not_13_out, B2);
  and and_11 (and_11_out, not_13_out, not_14_out);
  not not_14 (not_14_out, D);
  and and_12 (and_12_out, C, not_15_out);
  not not_15 (not_15_out, D);
  not not_16 (not_16_out, A);
  and and_13 (and_13_out, not_16_out, B2, C);
  not not_17 (not_17_out, B2);
  and and_14 (and_14_out, not_17_out, not_18_out);
  not not_18 (not_18_out, D);
  not not_19 (not_19_out, B2);
  and and_15 (and_15_out, not_19_out, C);
  and and_16 (and_16_out, C, not_20_out);
  not not_20 (not_20_out, D);
  not not_21 (not_21_out, C);
  and and_17 (and_17_out, B2, not_21_out, D);
  not not_22 (not_22_out, C);
  or or_1 (C2, not_22_out, D, B2);
  or or_2 (B, not_1_out, and_1_out, and_2_out);
  or or_3 (A2, and_3_out, C, and_4_out, A);
  or or_4 (F, and_5_out, and_6_out, and_7_out, A);
  or or_5 (G, and_8_out, and_9_out, and_10_out, A);
  or or_6 (E, and_11_out, and_12_out, and_13_out);
  or or_7 (D2, and_14_out, and_15_out, and_16_out, and_17_out, A);
endmodule

module soma (
  input  a,
  input  b,
  input  c,
  input  d,
  output s1,
  output s0,
  output carry_in,
  output carry_out
);

  wire and_1_out, and_2_out, and_3_out, and_4_out, and_5_out, and_6_out, and_7_out, and_8_out, and_9_out,
       and_10_out, and_11_out, not_1_out, not_2_out, not_3_out, not_4_out, not_5_out, not_6_out, not_7_out,
       not_8_out, not_9_out, not_10_out, not_11_out, not_12_out;

  not not_1 (not_1_out, a);
  not not_2 (not_2_out, b);
  not not_3 (not_3_out, a);
  not not_4 (not_4_out, d);
  not not_5 (not_5_out, a);
  not not_6 (not_6_out, c);
  not not_7 (not_7_out, b);
  not not_8 (not_8_out, c);
  not not_9 (not_9_out, c);
  not not_10 (not_10_out, d);
  not not_11 (not_11_out, b);
  and and_1 (and_1_out, not_11_out, d);
  and and_2 (and_2_out, b, not_12_out);
  not not_12 (not_12_out, d);
  and and_3 (and_3_out, b, c, d);
  and and_4 (and_4_out, a, c);
  and and_5 (and_5_out, a, b, d);
  and and_6 (and_6_out, not_1_out, not_2_out, c);
  and and_7 (and_7_out, not_3_out, c, not_4_out);
  and and_8 (and_8_out, not_5_out, b, not_6_out, d);
  and and_9 (and_9_out, a, not_7_out, not_8_out);
  and and_10 (and_10_out, a, not_9_out, not_10_out);
  and and_11 (and_11_out, a, b, c, d);
  or or_1 (s0, and_1_out, and_2_out);
  or or_2 (carry_out, and_3_out, and_4_out, and_5_out);
  or or_3 (s1, and_6_out, and_7_out, and_8_out, and_9_out, and_10_out, and_11_out);

  assign carry_in = 1'b0;
endmodule

module multiplica (
  input  a,
  input  b,
  input  c,
  input  d,
  output p3,
  output p2,
  output p1,
  output p0
);

  wire and_2_out, and_3_out, and_4_out, and_5_out, and_6_out, and_7_out, and_8_out, and_9_out, not_1_out,
       not_2_out, not_3_out, not_4_out, not_5_out, not_6_out;

  and and_1 (p3, a, b, c);
  not not_1 (not_1_out, b);
  and and_2 (and_2_out, a, not_1_out, c);
  and and_3 (and_3_out, a, b, d);
  not not_2 (not_2_out, a);
  and and_4 (and_4_out, not_2_out, b, c);
  and and_5 (and_5_out, a, not_3_out, d);
  not not_3 (not_3_out, b);
  and and_6 (and_6_out, a, b, not_4_out);
  not not_4 (not_4_out, c);
  and and_7 (and_7_out, a, b, not_5_out);
  not not_5 (not_5_out, d);
  and and_8 (and_8_out, b, d);
  and and_9 (and_9_out, a, b, not_6_out);
  not not_6 (not_6_out, c);
  or or_1 (p2, and_2_out, and_3_out);
  or or_2 (p1, and_4_out, and_5_out, and_6_out, and_7_out);
  or or_3 (p0, and_8_out, and_9_out);
endmodule
