// Logisim project TransmissaoSerialDeBits.circ as structural Verilog: 2 circuits, main circuit main
module main (
  input  in_1,
  input  in_2,
  input  in_3,
  input  in_4,
  input  in_5
);

  wire and_1_out, and_2_out, and_3_out, and_4_out, clock_1_out, d_ff_1_q, d_ff_2_q, d_ff_3_q, d_ff_4_q,
       d_ff_5_q, d_ff_6_q, d_ff_7_q, d_ff_8_q, d_ff_9_q, d_ff_10_q, d_ff_11_q, d_ff_12_q, d_ff_13_q,
       d_ff_14_q, d_ff_15_q, d_ff_16_q, or_1_out, seg_1_a, seg_1_b, seg_1_c, seg_1_d, seg_1_e, seg_1_f,
       seg_1_g, seg_2_a, seg_2_b, seg_2_c, seg_2_d, seg_2_e, seg_2_f, seg_2_g;

  Clock clock_1 (.out(clock_1_out));
  D_Flip_Flop d_ff_1 (.clk(clock_1_out), .D(d_ff_4_q), .Q(d_ff_1_q), .reset(in_1));  // open: Qn, preset, en
  seg seg_1 (
    .b1(in_2), .b2(in_3), .b3(in_4), .b4(in_5), .a(seg_1_a), .b(seg_1_b), .c(seg_1_c), .d(seg_1_d),
    .e(seg_1_e), .f(seg_1_f), .g(seg_1_g));
  _7_Segment_Display u_7_segment_display_1 (
    .g(seg_1_g), .f(seg_1_f), .a(seg_1_a), .b(seg_1_b), .e(seg_1_e), .d(seg_1_d), .c(seg_1_c));  // open: dp
  D_Flip_Flop d_ff_2 (.clk(clock_1_out), .D(d_ff_1_q), .Q(d_ff_2_q), .reset(in_1));  // open: Qn, preset, en
  and and_1 (and_1_out, d_ff_1_q, in_2);
  and and_2 (and_2_out, d_ff_2_q, in_3);
  D_Flip_Flop d_ff_3 (.clk(clock_1_out), .D(d_ff_2_q), .Q(d_ff_3_q), .reset(in_1));  // open: Qn, preset, en
  and and_3 (and_3_out, d_ff_3_q, in_4);
  D_Flip_Flop d_ff_4 (.clk(clock_1_out), .D(d_ff_3_q), .Q(d_ff_4_q), .reset(in_1));  // open: Qn, preset, en
  and and_4 (and_4_out, d_ff_4_q, in_5);
  or or_1 (or_1_out, and_1_out, and_2_out, and_3_out, and_4_out);
  D_Flip_Flop d_ff_5 (.clk(clock_1_out), .D(d_ff_13_q), .Q(d_ff_5_q), .preset(in_1));  // open: Qn, en, reset
  D_Flip_Flop d_ff_6 (.clk(clock_1_out), .D(or_1_out), .Q(d_ff_6_q));  // open: Qn, preset, en, reset
  D_Flip_Flop d_ff_7 (.clk(clock_1_out), .D(d_ff_5_q), .Q(d_ff_7_q), .reset(in_1));  // open: Qn, preset, en
  D_Flip_Flop d_ff_8 (.clk(clock_1_out), .D(d_ff_6_q), .Q(d_ff_8_q));  // open: Qn, preset, en, reset
  D_Flip_Flop d_ff_9 (.clk(d_ff_5_q), .D(d_ff_6_q), .Q(d_ff_9_q));  // open: Qn, preset, en, reset
  D_Flip_Flop d_ff_10 (.clk(clock_1_out), .D(d_ff_7_q), .Q(d_ff_10_q), .reset(in_1));  // open: Qn, preset, en
  D_Flip_Flop d_ff_11 (.clk(clock_1_out), .D(d_ff_8_q), .Q(d_ff_11_q));  // open: Qn, preset, en, reset
  D_Flip_Flop d_ff_12 (.clk(d_ff_5_q), .D(d_ff_8_q), .Q(d_ff_12_q));  // open: Qn, preset, en, reset
  seg seg_2 (
    .b1(d_ff_16_q), .b2(d_ff_15_q), .b3(d_ff_12_q), .b4(d_ff_9_q), .a(seg_2_a), .b(seg_2_b), .c(seg_2_c),
    .d(seg_2_d), .e(seg_2_e), .f(seg_2_f), .g(seg_2_g));
  _7_Segment_Display u_7_segment_display_2 (
    .g(seg_2_g), .f(seg_2_f), .a(seg_2_a), .b(seg_2_b), .e(seg_2_e), .d(seg_2_d), .c(seg_2_c));  // open: dp
  D_Flip_Flop d_ff_13 (.clk(clock_1_out), .D(d_ff_10_q), .Q(d_ff_13_q), .reset(in_1));  // open: Qn, preset, en
  D_Flip_Flop d_ff_14 (.clk(clock_1_out), .D(d_ff_11_q), .Q(d_ff_14_q));  // open: Qn, preset, en, reset
  D_Flip_Flop d_ff_15 (.clk(d_ff_5_q), .D(d_ff_11_q), .Q(d_ff_15_q));  // open: Qn, preset, en, reset
  D_Flip_Flop d_ff_16 (.clk(d_ff_5_q), .D(d_ff_14_q), .Q(d_ff_16_q));  // open: Qn, preset, en, reset
endmodule

module seg (
  input  b1,
  input  b2,
  input  b3,
  input  b4,
  output a,
  output b,
  output c,
  output d,
  output e,
  output f,
  output g
);

  wire and_1_out, and_2_out, and_3_out, and_4_out, and_5_out, and_6_out, and_7_out, and_8_out, and_9_out,
       and_10_out, and_11_out, and_12_out, and_13_out, and_14_out, and_15_out, and_16_out, and_17_out,
       and_18_out, and_19_out, and_20_out, and_21_out, and_22_out, and_23_out, and_24_out, and_25_out,
       and_26_out, and_27_out, and_28_out, and_29_out, and_30_out, and_31_out, and_32_out, and_33_out,
       and_34_out, and_35_out, not_1_out, not_2_out, not_3_out, not_4_out, not_5_out, not_6_out, not_7_out,
       not_8_out, not_9_out, not_10_out, not_11_out, not_12_out, not_13_out, not_14_out, not_15_out,
       not_16_out, not_17_out, not_18_out, not_19_out, not_20_out, not_21_out, not_22_out, not_23_out,
       not_24_out, not_25_out, not_26_out, not_27_out, not_28_out, not_29_out, not_30_out, not_31_out,
       not_32_out, not_33_out, not_34_out, not_35_out, not_36_out, not_37_out, not_38_out, not_39_out,
       not_40_out, not_41_out, not_42_out, not_43_out;

  not not_1 (not_1_out, b2);
  and and_1 (and_1_out, not_1_out, not_2_out);
  not not_2 (not_2_out, b4);
  not not_3 (not_3_out, b1);
  and and_2 (and_2_out, not_3_out, b3);
  not not_4 (not_4_out, b1);
  and and_3 (and_3_out, not_4_out, b2, b4);
  and and_4 (and_4_out, b2, b3);
  not not_5 (not_5_out, b2);
  and and_5 (and_5_out, b1, not_5_out, not_6_out);
  not not_6 (not_6_out, b3);
  and and_6 (and_6_out, b1, not_7_out);
  not not_7 (not_7_out, b4);
  not not_8 (not_8_out, b1);
  and and_7 (and_7_out, not_8_out, not_9_out);
  not not_9 (not_9_out, b2);
  not not_10 (not_10_out, b1);
  not not_11 (not_11_out, b3);
  and and_8 (and_8_out, not_10_out, not_11_out, not_12_out);
  not not_12 (not_12_out, b4);
  not not_13 (not_13_out, b2);
  and and_9 (and_9_out, not_13_out, not_14_out);
  not not_14 (not_14_out, b4);
  not not_15 (not_15_out, b1);
  and and_10 (and_10_out, not_15_out, b3, b4);
  not not_16 (not_16_out, b3);
  and and_11 (and_11_out, b1, not_16_out, b4);
  not not_17 (not_17_out, b1);
  and and_12 (and_12_out, not_17_out, not_18_out);
  not not_18 (not_18_out, b3);
  not not_19 (not_19_out, b1);
  and and_13 (and_13_out, not_19_out, b4);
  not not_20 (not_20_out, b3);
  and and_14 (and_14_out, not_20_out, b4);
  not not_21 (not_21_out, b1);
  and and_15 (and_15_out, not_21_out, b2);
  and and_16 (and_16_out, b1, not_22_out);
  not not_22 (not_22_out, b2);
  not not_23 (not_23_out, b1);
  and and_17 (and_17_out, not_23_out, not_24_out, not_25_out);
  not not_24 (not_24_out, b2);
  not not_25 (not_25_out, b4);
  not not_26 (not_26_out, b2);
  and and_18 (and_18_out, not_26_out, b3, b4);
  not not_27 (not_27_out, b3);
  and and_19 (and_19_out, b2, not_27_out, b4);
  and and_20 (and_20_out, b2, b3, not_28_out);
  not not_28 (not_28_out, b4);
  and and_21 (and_21_out, b1, not_29_out);
  not not_29 (not_29_out, b3);
  not not_30 (not_30_out, b2);
  and and_22 (and_22_out, not_30_out, not_31_out);
  not not_31 (not_31_out, b4);
  and and_23 (and_23_out, b3, not_32_out);
  not not_32 (not_32_out, b4);
  and and_24 (and_24_out, b1, b3);
  and and_25 (and_25_out, b1, b2);
  not not_33 (not_33_out, b3);
  and and_26 (and_26_out, not_33_out, not_34_out);
  not not_34 (not_34_out, b4);
  not not_35 (not_35_out, b1);
  and and_27 (and_27_out, not_35_out, b2, not_36_out);
  not not_36 (not_36_out, b3);
  and and_28 (and_28_out, b2, not_37_out);
  not not_37 (not_37_out, b4);
  and and_29 (and_29_out, b1, not_38_out);
  not not_38 (not_38_out, b2);
  and and_30 (and_30_out, b1, b3);
  not not_39 (not_39_out, b2);
  and and_31 (and_31_out, not_39_out, b3);
  and and_32 (and_32_out, b3, not_40_out);
  not not_40 (not_40_out, b4);
  not not_41 (not_41_out, b1);
  and and_33 (and_33_out, not_41_out, b2, not_42_out);
  not not_42 (not_42_out, b3);
  and and_34 (and_34_out, b1, not_43_out);
  not not_43 (not_43_out, b2);
  and and_35 (and_35_out, b1, b4);
  or or_1 (b, and_7_out, and_8_out, and_9_out, and_10_out, and_11_out);
  or or_2 (c, and_12_out, and_13_out, and_14_out, and_15_out, and_16_out);
  or or_3 (d, and_17_out, and_18_out, and_19_out, and_20_out, and_21_out);
  or or_4 (e, and_22_out, and_23_out, and_24_out, and_25_out);
  or or_5 (f, and_26_out, and_27_out, and_28_out, and_29_out, and_30_out);
  or or_6 (g, and_31_out, and_32_out, and_33_out, and_34_out, and_35_out);
  or or_7 (a, and_1_out, and_2_out, and_3_out, and_4_out, and_5_out, and_6_out);
endmodule
