// Logisim project calculadora.circ as structural Verilog: 4 circuits, main circuit main
module main (
  input  in_1,
  input  in_2,
  input  in_3,
  input  in_4,
  input  in_5,
  input  in_6,
  input  in_7,
  input  in_8
);

  wire and_1_out, and_2_out, and_3_out, and_4_out, and_5_out, and_6_out, and_7_out, and_8_out, and_9_out,
       and_10_out, multiplica_1_s1, multiplica_1_s2, multiplica_1_s3, multiplica_1_s4, or_1_out, or_2_out,
       or_3_out, or_4_out, seg_1_a, seg_1_b, seg_1_c, seg_1_d, seg_1_e, seg_1_f, seg_1_g, seg_2_a, seg_2_e,
       seg_2_f, seg_2_g, seg_3_a, seg_3_b, seg_3_c, seg_3_d, seg_3_e, seg_3_f, seg_3_g, soma_1_s1, soma_1_s2,
       soma_1_s3, soma_1_s4;

  seg seg_1 (
    .b1(in_7), .b2(in_7), .b3(in_3), .b4(in_4), .a(seg_1_a), .b(seg_1_b), .c(seg_1_c), .d(seg_1_d),
    .e(seg_1_e), .f(seg_1_f), .g(seg_1_g));
  _7_Segment_Display u_7_segment_display_1 (
    .g(seg_1_g), .f(seg_1_f), .a(seg_1_a), .b(seg_1_b), .e(seg_1_e), .d(seg_1_d), .c(seg_1_c));  // open: dp
  and and_1 (and_1_out, ~in_1, in_2);  // AND_Gate
  and and_2 (and_2_out, in_6, and_1_out);
  seg seg_2 (
    .b1(in_8), .b2(in_8), .b3(in_5), .b4(in_6), .a(seg_2_a), .b(seg_2_a), .c(seg_2_a), .d(seg_2_a),
    .e(seg_2_e), .f(seg_2_f), .g(seg_2_g));
  _7_Segment_Display u_7_segment_display_2 (
    .g(seg_2_g), .f(seg_2_f), .a(seg_2_a), .b(seg_2_a), .e(seg_2_e), .d(seg_2_a), .c(seg_2_a));  // open: dp
  and and_3 (and_3_out, in_5, and_1_out);
  and and_4 (and_4_out, in_3, and_1_out);
  and and_5 (and_5_out, in_4, and_1_out);
  multiplica multiplica_1 (
    .a1(and_4_out), .a2(and_5_out), .b1(and_3_out), .b2(and_2_out), .s1(multiplica_1_s1),
    .s2(multiplica_1_s2), .s3(multiplica_1_s3), .s4(multiplica_1_s4));
  or or_1 (or_1_out, multiplica_1_s4, soma_1_s4);
  or or_2 (or_2_out, multiplica_1_s3, soma_1_s3);
  _7_Segment_Display u_7_segment_display_3 (
    .g(seg_3_g), .f(seg_3_f), .a(seg_3_a), .b(seg_3_b), .e(seg_3_e), .d(seg_3_d), .c(seg_3_c));  // open: dp
  or or_3 (or_3_out, multiplica_1_s1, soma_1_s1);
  or or_4 (or_4_out, multiplica_1_s2, soma_1_s2);
  seg seg_3 (
    .b1(or_3_out), .b2(or_4_out), .b3(or_2_out), .b4(or_1_out), .a(seg_3_a), .b(seg_3_b), .c(seg_3_c),
    .d(seg_3_d), .e(seg_3_e), .f(seg_3_f), .g(seg_3_g));
  and and_6 (and_6_out, ~in_1, ~in_2);  // AND_Gate
  and and_7 (and_7_out, in_6, and_6_out);
  and and_8 (and_8_out, in_4, and_6_out);
  and and_9 (and_9_out, in_5, and_6_out);
  soma soma_1 (
    .a1(and_10_out), .a2(and_8_out), .b1(and_9_out), .b2(and_7_out), .s1(soma_1_s1), .s2(soma_1_s2),
    .s3(soma_1_s3), .s4(soma_1_s4));
  and and_10 (and_10_out, in_3, and_6_out);
endmodule

module multiplica (
  input  a1,
  input  a2,
  input  b1,
  input  b2,
  output s1,
  output s2,
  output s3,
  output s4
);

  wire and_2_out, and_3_out, and_4_out, and_5_out, and_6_out, and_7_out, not_1_out, not_2_out, not_3_out,
       not_4_out, not_5_out, not_6_out;

  and and_1 (s1, a1, a2, b1, b2);
  not not_1 (not_1_out, a2);
  and and_2 (and_2_out, a1, not_1_out, b1);
  and and_3 (and_3_out, a1, b1, not_2_out);
  not not_2 (not_2_out, b2);
  not not_3 (not_3_out, a1);
  and and_4 (and_4_out, not_3_out, a2, b1);
  and and_5 (and_5_out, a2, b1, not_4_out);
  not not_4 (not_4_out, b2);
  not not_5 (not_5_out, a2);
  and and_6 (and_6_out, a1, not_5_out, b2);
  not not_6 (not_6_out, b1);
  and and_7 (and_7_out, a1, not_6_out, b2);
  and and_8 (s4, a2, b2);
  or or_1 (s2, and_2_out, and_3_out);
  or or_2 (s3, and_4_out, and_5_out, and_6_out, and_7_out);
endmodule

module soma (
  input  a1,
  input  a2,
  input  b1,
  input  b2,
  output s1,
  output s2,
  output s3,
  output s4
);

  wire and_1_out, and_2_out, and_3_out, and_4_out, and_5_out, and_6_out, and_7_out, and_8_out, and_9_out,
       and_10_out, and_11_out, not_1_out, not_2_out, not_3_out, not_4_out, not_5_out, not_6_out, not_7_out,
       not_8_out, not_9_out, not_10_out, not_11_out, not_12_out;

  and and_1 (and_1_out, a2, b1, b2);
  and and_2 (and_2_out, a1, b1);
  and and_3 (and_3_out, a1, a2, b2);
  not not_1 (not_1_out, a1);
  not not_2 (not_2_out, a2);
  not not_3 (not_3_out, a1);
  not not_4 (not_4_out, b2);
  not not_5 (not_5_out, a1);
  not not_6 (not_6_out, b1);
  not not_7 (not_7_out, a2);
  not not_8 (not_8_out, b1);
  not not_9 (not_9_out, b1);
  not not_10 (not_10_out, b2);
  not not_11 (not_11_out, a2);
  and and_4 (and_4_out, not_11_out, b2);
  and and_5 (and_5_out, a2, not_12_out);
  not not_12 (not_12_out, b2);
  or or_1 (s2, and_1_out, and_2_out, and_3_out);
  and and_6 (and_6_out, not_1_out, not_2_out, b1);
  and and_7 (and_7_out, not_3_out, b1, not_4_out);
  and and_8 (and_8_out, not_5_out, a2, not_6_out, b2);
  and and_9 (and_9_out, a1, not_7_out, not_8_out);
  and and_10 (and_10_out, a1, not_9_out, not_10_out);
  and and_11 (and_11_out, a1, a2, b1, b2);
  or or_2 (s4, and_4_out, and_5_out);
  or or_3 (s3, and_6_out, and_7_out, and_8_out, and_9_out, and_10_out, and_11_out);

  assign s1 = 1'b0;
endmodule

module seg (
  input  b1,
  input  b2,
  input  b3,
  input  b4,
  output a,
  output b,
  output c,
  output d,
  output e,
  output f,
  output g
);

  wire and_1_out, and_2_out, and_3_out, and_4_out, and_5_out, and_6_out, and_7_out, and_8_out, and_9_out,
       and_10_out, and_11_out, and_12_out, and_13_out, and_14_out, and_15_out, and_16_out, and_17_out,
       and_18_out, and_19_out, and_20_out, and_21_out, and_22_out, and_23_out, and_24_out, and_25_out,
       and_26_out, and_27_out, and_28_out, and_29_out, and_30_out, and_31_out, and_32_out, and_33_out,
       and_34_out, and_35_out, not_1_out, not_2_out, not_3_out, not_4_out, not_5_out, not_6_out, not_7_out,
       not_8_out, not_9_out, not_10_out, not_11_out, not_12_out, not_13_out, not_14_out, not_15_out,
       not_16_out, not_17_out, not_18_out, not_19_out, not_20_out, not_21_out, not_22_out, not_23_out,
       not_24_out, not_25_out, not_26_out, not_27_out, not_28_out, not_29_out, not_30_out, not_31_out,
       not_32_out, not_33_out, not_34_out, not_35_out, not_36_out, not_37_out, not_38_out, not_39_out,
       not_40_out, not_41_out, not_42_out, not_43_out;

  not not_1 (not_1_out, b2);
  and and_1 (and_1_out, not_1_out, not_2_out);
  not not_2 (not_2_out, b4);
  not not_3 (not_3_out, b1);
  and and_2 (and_2_out, not_3_out, b3);
  not not_4 (not_4_out, b1);
  and and_3 (and_3_out, not_4_out, b2, b4);
  and and_4 (and_4_out, b2, b3);
  not not_5 (not_5_out, b2);
  and and_5 (and_5_out, b1, not_5_out, not_6_out);
  not not_6 (not_6_out, b3);
  and and_6 (and_6_out, b1, not_7_out);
  not not_7 (not_7_out, b4);
  not not_8 (not_8_out, b1);
  and and_7 (and_7_out, not_8_out, not_9_out);
  not not_9 (not_9_out, b2);
  not not_10 (not_10_out, b1);
  not not_11 (not_11_out, b3);
  and and_8 (and_8_out, not_10_out, not_11_out, not_12_out);
  not not_12 (not_12_out, b4);
  not not_13 (not_13_out, b2);
  and and_9 (and_9_out, not_13_out, not_14_out);
  not not_14 (not_14_out, b4);
  not not_15 (not_15_out, b1);
  and and_10 (and_10_out, not_15_out, b3, b4);
  not not_16 (not_16_out, b3);
  and and_11 (and_11_out, b1, not_16_out, b4);
  not not_17 (not_17_out, b1);
  and and_12 (and_12_out, not_17_out, not_18_out);
  not not_18 (not_18_out, b3);
  not not_19 (not_19_out, b1);
  and and_13 (and_13_out, not_19_out, b4);
  not not_20 (not_20_out, b3);
  and and_14 (and_14_out, not_20_out, b4);
  not not_21 (not_21_out, b1);
  and and_15 (and_15_out, not_21_out, b2);
  and and_16 (and_16_out, b1, not_22_out);
  not not_22 (not_22_out, b2);
  not not_23 (not_23_out, b1);
  not not_24 (not_24_out, b2);
  and and_17 (and_17_out, not_23_out, not_24_out, not_25_out);
  not not_25 (not_25_out, b4);
  not not_26 (not_26_out, b2);
  and and_18 (and_18_out, not_26_out, b3, b4);
  not not_27 (not_27_out, b3);
  and and_19 (and_19_out, b2, not_27_out, b4);
  and and_20 (and_20_out, b2, b3, not_28_out);
  not not_28 (not_28_out, b4);
  and and_21 (and_21_out, b1, not_29_out);
  not not_29 (not_29_out, b3);
  not not_30 (not_30_out, b2);
  and and_22 (and_22_out, not_30_out, not_31_out);
  not not_31 (not_31_out, b4);
  and and_23 (and_23_out, b3, not_32_out);
  not not_32 (not_32_out, b4);
  and and_24 (and_24_out, b1, b3);
  and and_25 (and_25_out, b1, b2);
  not not_33 (not_33_out, b3);
  and and_26 (and_26_out, not_33_out, not_34_out);
  not not_34 (not_34_out, b4);
  not not_35 (not_35_out, b1);
  and and_27 (and_27_out, not_35_out, b2, not_36_out);
  not not_36 (not_36_out, b3);
  and and_28 (and_28_out, b2, not_37_out);
  not not_37 (not_37_out, b4);
  and and_29 (and_29_out, b1, not_38_out);
  not not_38 (not_38_out, b2);
  and and_30 (and_30_out, b1, b3);
  not not_39 (not_39_out, b2);
  and and_31 (and_31_out, not_39_out, b3);
  and and_32 (and_32_out, b3, not_40_out);
  not not_40 (not_40_out, b4);
  not not_41 (not_41_out, b1);
  and and_33 (and_33_out, not_41_out, b2, not_42_out);
  not not_42 (not_42_out, b3);
  and and_34 (and_34_out, b1, not_43_out);
  not not_43 (not_43_out, b2);
  and and_35 (and_35_out, b1, b4);
  or or_1 (b, and_7_out, and_8_out, and_9_out, and_10_out, and_11_out);
  or or_2 (c, and_12_out, and_13_out, and_14_out, and_15_out, and_16_out);
  or or_3 (d, and_17_out, and_18_out, and_19_out, and_20_out, and_21_out);
  or or_4 (e, and_22_out, and_23_out, and_24_out, and_25_out);
  or or_5 (f, and_26_out, and_27_out, and_28_out, and_29_out, and_30_out);
  or or_6 (g, and_31_out, and_32_out, and_33_out, and_34_out, and_35_out);
  or or_7 (a, and_1_out, and_2_out, and_3_out, and_4_out, and_5_out, and_6_out);
endmodule
