// Logisim project circuitoram.circ as structural Verilog
module circuito (
  input  \Endereço ,
  input  in_2,
  input  Dados_a_serem_gravados,
  input  Controle
);

  wire and_1_out, and_2_out, and_3_out, and_4_out, and_5_out, and_6_out, and_7_out, and_8_out, and_9_out,
       and_10_out, and_11_out, and_12_out, and_13_out, and_14_out, and_15_out, and_16_out, not_1_out,
       or_1_out, s_r_ff_1_q, s_r_ff_2_q, s_r_ff_3_q, s_r_ff_4_q;

  not not_1 (not_1_out, Dados_a_serem_gravados);
  and and_1 (and_1_out, ~\Endereço , ~in_2);  // AND_Gate
  and and_2 (and_2_out, Dados_a_serem_gravados, and_1_out);
  and and_3 (and_3_out, ~\Endereço , in_2);  // AND_Gate
  S_R_Flip_Flop s_r_ff_1 (.S(and_2_out), .clk(Controle), .R(and_4_out), .Q(s_r_ff_1_q));  // open: Qn, preset, reset, en
  and and_4 (and_4_out, not_1_out, and_1_out);
  and and_5 (and_5_out, and_1_out, s_r_ff_1_q);
  and and_6 (and_6_out, \Endereço , ~in_2);  // AND_Gate
  and and_7 (and_7_out, Dados_a_serem_gravados, and_3_out);
  and and_8 (and_8_out, \Endereço , in_2);
  S_R_Flip_Flop s_r_ff_2 (.S(and_7_out), .clk(Controle), .R(and_9_out), .Q(s_r_ff_2_q));  // open: Qn, preset, reset, en
  and and_9 (and_9_out, not_1_out, and_3_out);
  and and_10 (and_10_out, and_3_out, s_r_ff_2_q);
  and and_11 (and_11_out, Dados_a_serem_gravados, and_6_out);
  and and_12 (and_12_out, not_1_out, and_6_out);
  S_R_Flip_Flop s_r_ff_3 (
    .S(and_11_out), .clk(Controle), .R(and_12_out), .Q(s_r_ff_3_q));  // open: Qn, preset, reset, en
  and and_13 (and_13_out, and_6_out, s_r_ff_3_q);
  and and_14 (and_14_out, Dados_a_serem_gravados, and_8_out);
  and and_15 (and_15_out, not_1_out, and_8_out);
  S_R_Flip_Flop s_r_ff_4 (
    .S(and_14_out), .clk(Controle), .R(and_15_out), .Q(s_r_ff_4_q));  // open: Qn, preset, reset, en
  and and_16 (and_16_out, and_8_out, s_r_ff_4_q);
  or or_1 (or_1_out, and_16_out, and_13_out, and_10_out, and_5_out);
endmodule
